# Fritzing sketch fritzing-obc (saved by Fritzing 0.9.9b)
breadboards: 1

parts:
  Part1 = Adafruit LSM9DS1 9DoF Breakout [part_number="Adafruit #3387"]
  Adafruit_HTS1 = Adafruit HTS221
  Raspberry_Pi_1 = Raspberry Pi 3 (updated for UniSat OBC) [part_number=RPI-3-V1.2]

nets:
  N1: Part1.SDA, Adafruit_HTS1.SDA, Raspberry_Pi_1.GPIO2
  N2: Part1.SCL, Adafruit_HTS1.SCL, Raspberry_Pi_1.GPIO3
  GND: Part1.GND, Adafruit_HTS1.GND, Raspberry_Pi_1.GND
  VDD: Part1.VDD, Raspberry_Pi_1.3V3

custom parts:
  Adafruit LSM9DS1 9DoF Breakout: Add motion, direction and orientation sensing to your Arduino project with this all-in-one 9-DOF sensor. Inside the chip are three sensors, one is a classic 3-axis accelerometer, which can tell you which direction is down towards the Earth (by measuring gravity) or how fast the board is accelerating in 3D space. The other is a 3-axis magnetometer that can sense where the strongest magnetic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
  Adafruit HTS221: Humidity is the concentration of water vapor (water when its a gas) in the air and for the most part it isn't something that you can see. Since you can't see humidity, if you care about how much there is, you'll have to measure it. This is where the HTS221 Temperature and Humidity Sensor by ST comes in. With a HTS221, you can take measurements of the relative humidity which can tell you how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
  Raspberry Pi 3 (updated for UniSat OBC): The RPi3, a faster version of the awesome Raspberry Pi 2 B ARM Board with 40 pin gpio. Ready for special Raspberry Pi B+ and RPi2 Hat (Hardware attached (on) top)
